# Fritzing sketch MegaRIOShield (saved by Fritzing 0.7.10b)
breadboards: 2

parts:
  J1 = female pin header, 14 pins [form="♀ (female)"]  # not connected
  J2 = female pin header, 14 pins [form="♀ (female)"]  # not connected
  J3 = female pin header, 14 pins [form="♀ (female)"]  # not connected
  J4 = female pin header, 8 pins [form="♀ (female)"]
  J5 = female pin header, 8 pins [form="♀ (female)"]  # not connected
  J6 = female pin header, 8 pins [form="♀ (female)"]  # not connected
  U1 = Arduino Mega  # not connected

nets:
  N1: J4.pin1, J4.pin2, J4.pin3, J4.pin4, J4.pin5, J4.pin7, J4.pin8
